# Fritzing sketch sahkomittari_nano_arduino (saved by Fritzing 0.9.3b)

parts:
  Part1 = Arduino Nano (Rev3.0) (ICSP)
  R1 = Resistor [tolerance=±5% resistance=3k package="0805 [SMD]"]
  Raspberry_Pi_1 = Raspberry Pi 3 [part_number=RPI-3-V1.2]
  DHT1 = DHT22 Humidity and Temperature Sensor
  JP1 = Header 3 [package=screwterminal-3.5mm-3_lock.007s]
  JP2 = Header 3 [package=screwterminal-3.5mm-3_lock.007s]
  R2 = Resistor [tolerance=±5% resistance=10k package=THT]
  R3 = Resistor [tolerance=±5% resistance=3k package="0805 [SMD]"]

nets:
  N1: Part1.D2, R1.Pin_0
  N2: Part1.GND, R1.Pin_1, R3.Pin_0
  N3: Part1.A0, R3.Pin_1
  3V3: Raspberry_Pi_1.3v3, Raspberry_Pi_1.3V3, JP2.1, R2.Pin_0
  N4: Raspberry_Pi_1.GIPO4, JP2.2, R2.Pin_1
  N5: Raspberry_Pi_1.GND, JP2.3
  N6: DHT1.VDD, JP1.1
  N7: DHT1.DATA, JP1.2
  N8: DHT1.GND, JP1.3

notes:
  7K8
  S0+
  S0-
  Sähkömittari
  10K
  palovar-signaali
